# Fritzing sketch trafic_light (saved by Fritzing 0.9.3b)
breadboards: 1

parts:
  LED1 = LED - 3mm [color="Green (555nm)" package="3 mm [THT]"]
  LED2 = LED - 3mm [color="Yellow (574nm)" package="3 mm [THT]"]
  LED3 = LED - 3mm [color="Red (633nm)" package="3 mm [THT]"]
  Composant1 = Arduino Uno (Rev3)
  R1 = Trimmer Potentiometer [maximum_resistance=10kΩ package=THT]

nets:
  N1: LED1.cathode, LED2.cathode, LED3.cathode, Composant1.GND, R1.leg2
  N2: LED1.anode, Composant1.D6_PWM
  N3: LED2.anode, Composant1.D5_PWM
  N4: LED3.anode, Composant1.D4
  N5: Composant1.A0, R1.wiper
  N6: Composant1.5V, R1.leg1
